# Fritzing sketch breadboarded (saved by Fritzing 0.8.3b)
breadboards: 1

parts:
  Part1 = Arduino Uno (Rev3)
  Raspberry_Pi_rev1 = Raspberry Pi rev2
  R1 = Resistor [tolerance=±5% resistance=1k package=THT]
  R2 = Resistor [tolerance=±5% resistance=2.2k package=THT]

nets:
  GND: Part1.GND, Raspberry_Pi_rev1.GND, R2.Pin_1
  5V: Part1.5V, Raspberry_Pi_rev1.5V
  N1: Part1.D0/RX, Raspberry_Pi_rev1.GPIO_14
  N2: Part1.D1/TX, R1.Pin_0
  N3: Raspberry_Pi_rev1.GPIO_15, Raspberry_Pi_rev1.GPIO_18, R1.Pin_1, R2.Pin_0
